// Logisim project dmux.circ as structural Verilog: 1 circuit, main circuit main
module main (
  input  In,
  input  Sel,
  output A,
  output B
);

  wire XOR_out;

  xor XOR (XOR_out, In, Sel);
  and And (A, In, XOR_out);
  and And_2 (B, In, Sel);
endmodule
